# Fritzing sketch arduino-uno-to-mega (saved by Fritzing 0.9.1b)

parts:
  Part1 = Arduino Uno (Rev3)
  Part2 = Arduino Mega 2560 (Rev3)

nets:
  N1: Part1.A5/SCL, Part2.D21/SCL
  GND: Part1.GND, Part2.GND
  N2: Part1.A4/SDA, Part2.D20/SDA, Part2.SDA

notes:
  Connect A0-A3, A6-A15 to any analog sensors
  Master.
  Running a variant of StandardFirmata or some custom Arduino sketch
  Slave.
  Running arduino_adc.ino
