# Fritzing sketch arduino-uno-to-micro (saved by Fritzing 0.9.1b)

parts:
  Part1 = Arduino Uno (Rev3)
  Part3 = Arduino Micro (Rev3)

nets:
  GND: Part1.GND, Part3.GND
  N1: Part1.A4/SDA, Part3.D2/SDA
  N2: Part1.A5/SCL, Part3.D3/SCL

notes:
  Connect A0-A5 to any analog sensors
  Master.
  Running a variant of StandardFirmata or some custom Arduino sketch
  Slave.
  Running arduino_adc.ino
