# Fritzing sketch arduino-uno-to-uno (saved by Fritzing 0.9.1b)

parts:
  Part1 = Arduino Uno (Rev3)
  Part2 = Arduino Uno (Rev3) - ICSP

nets:
  GND: Part1.GND, Part2.GND
  N1: Part1.A4/SDA, Part2.A4/SDA
  N2: Part1.A5/SCL, Part2.A5/SCL

notes:
  Connect A0-A3 to any analog sensors
  Master.
  Running a variant of StandardFirmata or some custom Arduino sketch
  Slave.
  Running arduino_adc.ino
